// Logisim project control_logic.circ as structural Verilog: 1 circuit, main circuit control_logic
module control_logic (
  input  [31:0] inst,
  input  BrEq,
  input  BrLt,
  input  [2:0] in_4,
  input  [2:0] in_5,
  input  [2:0] in_6,
  input  [2:0] in_7,
  input  [2:0] in_8,
  input  [2:0] in_9,
  input  [2:0] in_10,
  input  [2:0] in_11,
  input  [2:0] in_12,
  input  [2:0] in_13,
  input  [2:0] in_14,
  output PCSel,
  output RegWEn,
  output [2:0] ImmSel,
  output BrUn,
  output ASel,
  output BSel,
  output [3:0] ALUSel,
  output MemRW,
  output [1:0] WBSel,
  output CSRSel,
  output CSRWen,
  output SB,
  output SH,
  output SW,
  output LB,
  output LH,
  output LW,
  output [2:0] out_32
);

  wire and_7_out, and_8_out, and_9_out, and_10_out, and_11_out, and_12_out, and_13_out, comparator_1_eq,
       comparator_2_eq, comparator_3_eq, comparator_4_eq, comparator_5_eq, comparator_6_eq, comparator_7_eq,
       comparator_8_eq, comparator_11_eq, comparator_12_eq, comparator_13_eq, comparator_14_eq,
       comparator_17_eq, comparator_18_eq, comparator_20_eq, comparator_21_eq, comparator_25_eq,
       comparator_26_eq, comparator_31_eq, comparator_32_eq, comparator_33_eq, comparator_34_eq,
       comparator_35_eq, comparator_36_eq, comparator_38_eq, comparator_39_eq, comparator_40_eq,
       comparator_41_eq, comparator_42_eq, comparator_43_eq, Is_AUIPC, Is_B_Type, Is_I_ALU, Is_I_Type,
       Is_J_Type, Is_JAL, Is_JALR, Is_LOAD, Is_LUI, IS_MUL, IS_MULH, Is_R_Type, IS_SRA, IS_SUB, Is_U_Type,
       not_1_out, not_2_out, not_3_out, or_1_out, or_3_out, or_6_out, or_7_out, or_9_out;
  wire [1:0] multiplexer_14_out, multiplexer_15_out;
  wire [2:0] multiplexer_6_out, multiplexer_7_out, multiplexer_9_out, multiplexer_11_out, multiplexer_12_out;
  wire [3:0] ALUSel_RI, multiplexer_1_out, multiplexer_2_out, multiplexer_3_out, multiplexer_4_out,
       multiplexer_8_out;

  Comparator #(.width(3)) comparator_1 (.a(inst[14:12]), .b(3'b000), .eq(comparator_1_eq));  // open: gt, lt
  Comparator #(.width(7)) comparator_2 (.a(inst[31:25]), .b(7'b0000001), .eq(comparator_2_eq));  // open: gt, lt
  Comparator #(.width(3)) comparator_3 (.a(inst[14:12]), .b(3'b000), .eq(comparator_3_eq));  // open: gt, lt
  Comparator #(.width(7)) comparator_4 (.a(inst[31:25]), .b(7'b0100000), .eq(comparator_4_eq));  // open: gt, lt
  Comparator #(.width(3)) comparator_5 (.a(inst[14:12]), .b(3'b001), .eq(comparator_5_eq));  // open: gt, lt
  Comparator #(.width(7)) comparator_6 (.a(inst[31:25]), .b(7'b0000001), .eq(comparator_6_eq));  // open: gt, lt
  Comparator #(.width(3)) comparator_7 (.a(inst[14:12]), .b(3'b101), .eq(comparator_7_eq));  // open: gt, lt
  Comparator #(.width(7)) comparator_8 (.a(inst[31:25]), .b(7'b0100000), .eq(comparator_8_eq));  // open: gt, lt
  or or_1 (or_1_out, Is_R_Type, Is_I_ALU);
  and and_1 (IS_MUL, comparator_1_eq, comparator_2_eq, Is_R_Type);
  and and_2 (IS_SUB, comparator_3_eq, comparator_4_eq, Is_R_Type);
  and and_3 (IS_MULH, comparator_5_eq, comparator_6_eq, Is_R_Type);
  and and_4 (IS_SRA, comparator_7_eq, comparator_8_eq, or_1_out);
  Comparator #(.width(7)) comparator_9 (.a(inst[6:0]), .b(7'b0110011), .eq(Is_R_Type));  // open: gt, lt
  Comparator #(.width(7)) comparator_10 (.a(inst[6:0]), .b(7'b0010011), .eq(Is_I_ALU));  // open: gt, lt
  Comparator #(.width(7)) comparator_11 (.a(inst[6:0]), .b(7'b0000011), .eq(comparator_11_eq));  // open: gt, lt
  Comparator #(.width(7)) comparator_12 (.a(inst[6:0]), .b(7'b0010011), .eq(comparator_12_eq));  // open: gt, lt
  Comparator #(.width(7)) comparator_13 (.a(inst[6:0]), .b(7'b1100111), .eq(comparator_13_eq));  // open: gt, lt
  Comparator #(.width(7)) comparator_14 (.a(inst[6:0]), .b(7'b1110011), .eq(comparator_14_eq));  // open: gt, lt
  Comparator #(.width(7)) comparator_15 (.a(inst[6:0]), .b(7'b0100011), .eq(MemRW));  // open: gt, lt
  Comparator #(.width(7)) comparator_16 (.a(inst[6:0]), .b(7'b1100011), .eq(Is_B_Type));  // open: gt, lt
  Comparator #(.width(7)) comparator_17 (.a(inst[6:0]), .b(7'b0010111), .eq(comparator_17_eq));  // open: gt, lt
  Comparator #(.width(7)) comparator_18 (.a(inst[6:0]), .b(7'b0110111), .eq(comparator_18_eq));  // open: gt, lt
  Comparator #(.width(7)) comparator_19 (.a(inst[6:0]), .b(7'b1101111), .eq(Is_J_Type));  // open: gt, lt
  Comparator #(.width(7)) comparator_20 (.a(inst[6:0]), .b(7'b1110011), .eq(comparator_20_eq));  // open: gt, lt
  Comparator #(.width(3)) comparator_21 (.a(inst[14:12]), .b(3'b101), .eq(comparator_21_eq));  // open: gt, lt
  Multiplexer #(.enable("false"), .select(3), .width(4)) multiplexer_1 (
    .in0(4'b0000), .in1(4'b0110), .in2(4'b0111), .in3(4'b1011), .in4(4'b0011), .in5(4'b0100), .in6(4'b0010),
    .in7(4'b0001), .out(multiplexer_1_out), .sel(inst[14:12]));
  or or_2 (Is_U_Type, comparator_17_eq, comparator_18_eq);
  and and_5 (CSRSel, comparator_20_eq, comparator_21_eq);
  or or_3 (or_3_out, Is_R_Type, Is_I_ALU);
  or or_4 (Is_I_Type, comparator_11_eq, comparator_12_eq, comparator_13_eq, comparator_14_eq);
  Multiplexer #(.enable("false"), .width(4)) multiplexer_2 (
    .in0(multiplexer_1_out), .in1(4'b1010), .out(multiplexer_2_out), .sel(IS_MUL));
  Multiplexer #(.enable("false"), .width(4)) multiplexer_3 (
    .in0(4'b0000), .in1(ALUSel_RI), .out(multiplexer_3_out), .sel(or_3_out));
  Multiplexer #(.enable("false"), .width(4)) multiplexer_4 (
    .in0(multiplexer_2_out), .in1(4'b1100), .out(multiplexer_4_out), .sel(IS_SUB));
  Multiplexer #(.enable("false"), .width(4)) multiplexer_5 (
    .in0(multiplexer_3_out), .in1(4'b1101), .out(ALUSel), .sel(Is_LUI));
  Multiplexer #(.enable("false"), .width(3)) multiplexer_6 (
    .in0(3'b000), .in1(3'b000), .out(multiplexer_6_out), .sel(Is_I_Type));
  Multiplexer #(.enable("false"), .width(3)) multiplexer_7 (
    .in0(3'b000), .in1(3'b001), .out(multiplexer_7_out), .sel(MemRW));
  Multiplexer #(.enable("false"), .width(4)) multiplexer_8 (
    .in0(multiplexer_4_out), .in1(4'b1110), .out(multiplexer_8_out), .sel(IS_MULH));
  Multiplexer #(.enable("false"), .width(3)) multiplexer_9 (
    .in0(multiplexer_7_out), .in1(3'b010), .out(multiplexer_9_out), .sel(Is_B_Type));
  Multiplexer #(.enable("false"), .width(4)) multiplexer_10 (
    .in0(multiplexer_8_out), .in1(4'b0101), .out(ALUSel_RI), .sel(IS_SRA));
  Multiplexer #(.enable("false"), .width(3)) multiplexer_11 (
    .in0(multiplexer_9_out), .in1(3'b011), .out(multiplexer_11_out), .sel(Is_U_Type));
  Multiplexer #(.enable("false"), .width(3)) multiplexer_12 (
    .in0(multiplexer_11_out), .in1(3'b100), .out(multiplexer_12_out), .sel(Is_J_Type));
  Multiplexer #(.enable("false"), .width(3)) multiplexer_13 (
    .in0(multiplexer_12_out), .in1(3'b101), .out(ImmSel), .sel(CSRSel));
  Multiplexer #(.enable("false"), .width(2)) multiplexer_14 (
    .in0(2'b01), .in1(2'b00), .out(multiplexer_14_out), .sel(Is_LOAD));
  Comparator #(.width(7)) comparator_22 (.a(inst[6:0]), .b(7'b0100011), .eq(MemRW));  // open: gt, lt
  nor nor_1 (RegWEn, MemRW, Is_B_Type);
  Comparator #(.width(7)) comparator_23 (.a(inst[6:0]), .b(7'b1101111), .eq(Is_J_Type));  // open: gt, lt
  Comparator #(.width(7)) comparator_24 (.a(inst[6:0]), .b(7'b0010111), .eq(Is_AUIPC));  // open: gt, lt
  or or_5 (ASel, Is_B_Type, Is_J_Type, Is_AUIPC);
  Multiplexer #(.enable("false"), .width(2)) multiplexer_15 (
    .in0(multiplexer_14_out), .in1(2'b10), .out(multiplexer_15_out), .sel(or_6_out));
  or or_6 (or_6_out, Is_JAL, Is_JALR);
  Multiplexer #(.enable("false"), .width(2)) multiplexer_16 (
    .in0(multiplexer_15_out), .in1(2'b11), .out(WBSel), .sel(CSRWen));
  Comparator #(.width(3)) comparator_25 (.a(inst[14:12]), .b(3'b110), .eq(comparator_25_eq));  // open: gt, lt
  Comparator #(.width(3)) comparator_26 (.a(inst[14:12]), .b(3'b111), .eq(comparator_26_eq));  // open: gt, lt
  Comparator #(.width(7)) comparator_27 (.a(inst[6:0]), .b(7'b0000011), .eq(Is_LOAD));  // open: gt, lt
  Comparator #(.width(7)) comparator_28 (.a(inst[6:0]), .b(7'b0110111), .eq(Is_LUI));  // open: gt, lt
  Comparator #(.width(7)) comparator_29 (.a(inst[6:0]), .b(7'b1101111), .eq(Is_JAL));  // open: gt, lt
  Comparator #(.width(7)) comparator_30 (.a(inst[6:0]), .b(7'b1100111), .eq(Is_JALR));  // open: gt, lt
  or or_7 (or_7_out, comparator_25_eq, comparator_26_eq);
  Comparator #(.width(3)) comparator_31 (.a(inst[14:12]), .b(3'b000), .eq(comparator_31_eq));  // open: gt, lt
  Comparator #(.width(3)) comparator_32 (.a(inst[14:12]), .b(3'b001), .eq(comparator_32_eq));  // open: gt, lt
  not not_1 (not_1_out, BrEq);
  Comparator #(.width(3)) comparator_33 (.a(inst[14:12]), .b(3'b100), .eq(comparator_33_eq));  // open: gt, lt
  Comparator #(.width(3)) comparator_34 (.a(inst[14:12]), .b(3'b101), .eq(comparator_34_eq));  // open: gt, lt
  not not_2 (not_2_out, BrLt);
  Comparator #(.width(3)) comparator_35 (.a(inst[14:12]), .b(3'b110), .eq(comparator_35_eq));  // open: gt, lt
  Comparator #(.width(3)) comparator_36 (.a(inst[14:12]), .b(3'b111), .eq(comparator_36_eq));  // open: gt, lt
  not not_3 (not_3_out, BrLt);
  and and_6 (BrUn, Is_B_Type, or_7_out);
  and and_7 (and_7_out, comparator_31_eq, BrEq);
  and and_8 (and_8_out, comparator_32_eq, not_1_out);
  and and_9 (and_9_out, comparator_33_eq, BrLt);
  and and_10 (and_10_out, comparator_34_eq, not_2_out);
  and and_11 (and_11_out, comparator_35_eq, BrLt);
  and and_12 (and_12_out, comparator_36_eq, not_3_out);
  or or_8 (BSel, Is_I_ALU, Is_B_Type, Is_AUIPC, Is_LOAD, Is_LUI, Is_JAL, Is_JALR);
  or or_9 (or_9_out, and_7_out, and_8_out, and_9_out, and_10_out, and_11_out, and_12_out);
  Comparator #(.width(7)) comparator_37 (.a(inst[6:0]), .b(7'b1110011), .eq(CSRWen));  // open: gt, lt
  and and_13 (and_13_out, Is_B_Type, or_9_out);
  or or_10 (PCSel, and_13_out, Is_JAL, Is_JALR);
  Comparator #(.width(3)) comparator_38 (.a(inst[14:12]), .b(3'b000), .eq(comparator_38_eq));  // open: gt, lt
  Comparator #(.width(3)) comparator_39 (.a(inst[14:12]), .b(3'b001), .eq(comparator_39_eq));  // open: gt, lt
  Comparator #(.width(3)) comparator_40 (.a(inst[14:12]), .b(3'b010), .eq(comparator_40_eq));  // open: gt, lt
  Comparator #(.width(3)) comparator_41 (.a(inst[14:12]), .b(3'b000), .eq(comparator_41_eq));  // open: gt, lt
  Comparator #(.width(3)) comparator_42 (.a(inst[14:12]), .b(3'b001), .eq(comparator_42_eq));  // open: gt, lt
  Comparator #(.width(3)) comparator_43 (.a(inst[14:12]), .b(3'b010), .eq(comparator_43_eq));  // open: gt, lt
  and and_14 (LB, Is_LOAD, comparator_38_eq);
  and and_15 (LH, Is_LOAD, comparator_39_eq);
  and and_16 (LW, Is_LOAD, comparator_40_eq);
  and and_17 (SB, MemRW, comparator_41_eq);
  and and_18 (SH, MemRW, comparator_42_eq);
  and and_19 (SW, MemRW, comparator_43_eq);
  Multiplexer #(.enable("false"), .width(3)) multiplexer_17 (.in0(3'b000), .in1(3'b000), .out(in_4), .sel(Is_I_Type));
  Multiplexer #(.enable("false"), .width(3)) multiplexer_18 (.in0(3'b000), .in1(3'b001), .out(in_6), .sel(MemRW));
  Multiplexer #(.enable("false"), .width(3)) multiplexer_19 (.in0(3'b000), .in1(3'b010), .out(in_9), .sel(Is_B_Type));
  Multiplexer #(.enable("false"), .width(3)) multiplexer_20 (.in0(3'b000), .in1(3'b011), .out(in_11), .sel(Is_U_Type));
  Multiplexer #(.enable("false"), .width(3)) multiplexer_21 (.in0(3'b000), .in1(3'b100), .out(in_13), .sel(Is_J_Type));
  Multiplexer #(.enable("false"), .width(3)) multiplexer_22 (.in0(3'b000), .in1(3'b101), .out(in_14), .sel(CSRSel));
  Adder #(.width(3)) adder_1 (.a(in_4), .b(in_6), .out(in_5));  // open: cin, cout
  Adder #(.width(3)) adder_2 (.a(in_9), .b(in_11), .out(in_8));  // open: cin, cout
  Adder #(.width(3)) adder_3 (.a(in_13), .b(in_14), .out(in_12));  // open: cin, cout
  Adder #(.width(3)) adder_4 (.a(in_5), .b(in_8), .out(in_7));  // open: cin, cout
  Adder #(.width(3)) adder_5 (.a(in_7), .b(in_12), .out(in_10));  // open: cin, cout

  assign out_32 = ImmSel;

  // Other names for the same wires on the sheet: OPCode[6:0] = inst[6:0]; funct3[2:0] = inst[14:12];
  //   funct7[6:0] = inst[31:25]; Is_CSR = CSRWen; Is_CSRWI_Type = CSRSel; Is_S_Type = MemRW

  // Notes on the sheet:
  //   INPUTS to your circuit
  //   Instruction Decode
  //   ImmSel
  //   ALUSel：除了R和I类型指令以及LUI外其他类型的命令都是直接加法即可（LUI是直连）
  //   DON'T CHANGE THE LOCATIONS OF THE INPUTS AND OUTPUTS!
  //   OUTPUT from your circuit
  //   R和I类型的各个命令根据funct3调用不同ALU，funct7就只适用于区别R中的部分命令以及I中的两个移位命令
  //   RegWen
  //   ASel
  //   MemRW
  //   WBSel
  //   BrUn
  //   BSel
  //   PCSel
  //   CSR (Control State Register)
  //   Memory
endmodule
