// Logisim project cpu.circ as structural Verilog: 1 circuit, main circuit cpu
module cpu (
  input  clk,
  input  [31:0] INSTRUCTION,
  input  [31:0] READ_DATA,
  output [31:0] WRITE_ADDRESS,
  output [31:0] PROGRAM_COUNTER,
  output [31:0] ra,
  output [31:0] sp,
  output [31:0] t0,
  output [31:0] t1,
  output [31:0] t2,
  output [31:0] s0,
  output [31:0] s1,
  output [31:0] a0,
  output [31:0] tohost,
  output [3:0] WRITE_ENABLE,
  output [31:0] WRITE_DATA,
  output [31:0] out_17,
  output [31:0] out_18
);

  wire ASel, BrEq, BrLt, BrUn, BSel, CSRSel, CSRWen, LB, LH, LW, MemRW, PCSel, RegWen, SB, SH, SW;
  wire [1:0] WBSel;
  wire [2:0] ImmSel;
  wire [3:0] ALUSel, multiplexer_6_out;
  wire [31:0] adder_1_out, adder_2_out, ALUOUT, bit_extender_1_out, bit_extender_2_out, dataD, INSTRUCTION_R,
       MEMOUT, multiplexer_1_out, multiplexer_3_out, multiplexer_4_out, multiplexer_5_out,
       PIPELINED_INSTRUCTION, PROGRAM_COUNTER_R, READ_DATA1;

  Adder #(.width(32)) adder_1 (.a(out_17), .b(32'h4), .out(adder_1_out));  // open: cin, cout
  Multiplexer #(.enable("false"), .width(32)) multiplexer_1 (
    .in0(adder_1_out), .in1(ALUOUT), .out(multiplexer_1_out), .sel(PCSel));
  Multiplexer #(.enable("false"), .width(32)) multiplexer_2 (
    .in0(INSTRUCTION), .in1(32'h13), .out(PIPELINED_INSTRUCTION), .sel(PCSel));
  Register #(.width(32)) PC (.D(multiplexer_1_out), .clk(clk), .Q(out_17));  // open: en, clr
  imm_gen imm_gen_1 (.inst(INSTRUCTION_R), .ImmSel(ImmSel), .imm(out_18));
  control_logic control_logic_1 (
    .CSRWen(CSRWen), .SB(SB), .SH(SH), .SW(SW), .LB(LB), .LH(LH), .LW(LW), .PCSel(PCSel), .RegWEn(RegWen),
    .ImmSel(ImmSel), .BrUn(BrUn), .ASel(ASel), .BSel(BSel), .ALUSel(ALUSel), .MemRW(MemRW), .WBSel(WBSel),
    .CSRSel(CSRSel), .inst(INSTRUCTION_R), .BrEq(BrEq), .BrLt(BrLt));  // open: in_4
  Register #(.width(32)) register_1 (.D(PIPELINED_INSTRUCTION), .clk(clk), .Q(INSTRUCTION_R));  // open: en, clr
  regfile regfile_1 (
    .rs1(INSTRUCTION_R[19:15]), .rs2(INSTRUCTION_R[24:20]), .rd(INSTRUCTION_R[11:7]), .Write_Data(dataD),
    .RegWEn(RegWen), .clk(clk), .ra(ra), .sp(sp), .t0(t0), .t1(t1), .t2(t2), .s0(s0), .s1(s1), .a0(a0),
    .Read_Data_1(READ_DATA1), .Read_Data_2(WRITE_DATA));
  branch_comp branch_comp_1 (.rs1(READ_DATA1), .rs2(WRITE_DATA), .BrUn(BrUn), .BrEq(BrEq), .BrLt(BrLt));
  Multiplexer #(.enable("false"), .width(32)) multiplexer_3 (
    .in0(READ_DATA1), .in1(out_18), .out(multiplexer_3_out), .sel(CSRSel));
  Multiplexer #(.enable("false"), .width(32)) multiplexer_4 (
    .in0(READ_DATA1), .in1(PROGRAM_COUNTER_R), .out(multiplexer_4_out), .sel(ASel));
  Multiplexer #(.enable("false"), .width(32)) multiplexer_5 (
    .in0(WRITE_DATA), .in1(out_18), .out(multiplexer_5_out), .sel(BSel));
  Register #(.width(32)) register_2 (.D(out_17), .clk(clk), .Q(PROGRAM_COUNTER_R));  // open: en, clr
  alu alu_1 (.Result(ALUOUT), .A(multiplexer_4_out), .B(multiplexer_5_out), .ALUSel(ALUSel));
  csr csr_1 (
    .CSR_address(INSTRUCTION_R[31:20]), .CSR_din(multiplexer_3_out), .CSR_WE(CSRWen), .clk(clk),
    .tohost(tohost));
  Adder #(.width(32)) adder_2 (.a(32'h4), .b(PROGRAM_COUNTER_R), .out(adder_2_out));  // open: cin, cout
  Multiplexer #(.enable("false"), .select(2), .width(4)) multiplexer_6 (
    .in0(4'b1111), .in1(4'b0001), .in2(4'b0011), .out(multiplexer_6_out), .sel({SH, SB}));  // open: in3
  assign bit_extender_1_out = {{24{READ_DATA[7]}}, READ_DATA[7:0]};  // Bit_Extender bit_extender_1
  assign bit_extender_2_out = {{16{READ_DATA[15]}}, READ_DATA[15:0]};  // Bit_Extender bit_extender_2
  Multiplexer #(.enable("false"), .select(2), .width(32)) multiplexer_7 (
    .in0(MEMOUT), .in1(ALUOUT), .in2(adder_2_out), .in3(tohost), .out(dataD), .sel(WBSel));
  Multiplexer #(.enable("false"), .width(4)) multiplexer_8 (
    .in0(4'b0000), .in1(multiplexer_6_out), .out(WRITE_ENABLE), .sel(MemRW));
  Multiplexer #(.enable("false"), .select(2), .width(32)) multiplexer_9 (
    .in0(READ_DATA), .in1(bit_extender_1_out), .in2(bit_extender_2_out), .out(MEMOUT), .sel({LH, LB}));  // open: in3

  assign PROGRAM_COUNTER = out_17;

  // Other names for the same wires on the sheet: imme[31:0] = out_18; READ_DATA2[31:0] = WRITE_DATA

  // Notes on the sheet:
  //   Output to IMEM
  //   IMEM (do **NOT** move this)
  //   Inputs from IMEM
  //   It is OK to move the PC, RegFile, ALU, MEM, Branch Comp, Imm Gen, and Control Logic to wherever is most convenient for you when constructing your CPU, and to delete this text
  //   Inputs/Outputs for testing. Do **NOT** move these.
  //   Outputs To DMEM
  //   DMEM (do **NOT** move this)
  //   Inputs From DMEM
endmodule
