// Logisim project imm_gen.circ as structural Verilog: 1 circuit, main circuit imm_gen
module imm_gen (
  input  [31:0] inst,
  input  [2:0] ImmSel,
  output [31:0] imm,
  output [19:0] out_4,
  output [31:0] out_5
);

  wire [31:0] B_TYPE, CSRRWI_TYPE, I_TYPE, J_TYPE, S_TYPE;

  assign I_TYPE = {{20{inst[31]}}, inst[31:20]};  // Bit_Extender bit_extender_1
  assign S_TYPE = {{20{inst[31]}}, {inst[31:25], inst[11:7]}};  // Bit_Extender bit_extender_2
  assign B_TYPE = {{19{inst[31]}}, {inst[31], inst[7], inst[30:25], inst[11:8], 1'b0}};  // Bit_Extender bit_extender_3
  assign J_TYPE = {{11{inst[31]}}, {inst[31], inst[19:12], inst[20], inst[30:21], 1'b0}};  // Bit_Extender bit_extender_4
  assign CSRRWI_TYPE = {{27{1'b0}}, inst[19:15]};  // Bit_Extender bit_extender_5
  Multiplexer #(.enable("false"), .select(3), .width(32)) multiplexer_1 (
    .in0(I_TYPE), .in1(S_TYPE), .in2(B_TYPE), .in3({inst[31:12], {12{1'b0}}}), .in4(J_TYPE),
    .in5(CSRRWI_TYPE), .out(imm), .sel(ImmSel));  // open: in6, in7

  assign out_4 = inst[31:12];
  assign out_5 = {inst[31:12], {12{1'b0}}};

  // Other names for the same wires on the sheet: U_TYPE[31:12] = inst[31:12]

  // Notes on the sheet:
  //   INPUTS to your circuit
  //   DON'T CHANGE THE LOCATIONS OF THE INPUTS AND OUTPUTS!
  //   OUTPUT from your circuit
endmodule
